# Fritzing sketch RobotDiagram (saved by Fritzing 0.9.9b)

parts:
  Part1 = Adafruit LSM303DLHC Triple-axis Accelerometer+Magnetometer (Compass) [part_number="Adafruit #1120"]
  Part2 = Arduino Uno (Rev3)
  Part3 = GY-VL53L0XV2 Laser Ranger Module
  L298N1 = L298N DC motor driver
  M1 = DC Motor [part_number="12V DC Motor"]
  M2 = DC Motor [part_number="12V DC Motor"]

nets:
  N1: Part1.SCL, Part2.A5/SCL, Part3.SCL
  N2: Part1.SDA, Part2.A4/SDA, Part3.SDA
  GND: Part1.GND, Part2.GND, Part3.GND
  VIN: Part1.VIN, Part2.5V, Part3.VCC
  N3: Part2.D8, L298N1.IN1
  N4: Part2.D9_PWM, L298N1.ENA
  N5: Part2.D3_PWM, L298N1.ENB
  N6: Part2.D4, L298N1.IN3
  N7: Part2.D5_PWM, L298N1.IN4
  N8: Part2.D7, L298N1.IN2
  N9: L298N1.OUT1, M1.pin_1
  N10: L298N1.OUT2, M1.pin_2
  N11: L298N1.OUT3, M2.pin_2
  N12: L298N1.OUT4, M2.pin_1

notes:
  12v battery
  SDA == A4
  SCL == A5

custom parts:
  Adafruit LSM303DLHC Triple-axis Accelerometer+Magnetometer (Compass): He told you "Go West, young maker!" - but you don't know which way is West! Ah, if only you had this triple-axis accelerometer/magnetometer compass module. Inside are two sensors, one is a classic 3-axis accelerometer, which can tell you which direction is down towards the Earth (by measuring gravity). The other is a magnetometer that can sense where the strongest magnetic force is coming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
  GY-VL53L0XV2 Laser Ranger Module: The GY-VL53L0XV2 is based on the VL53L0X from ST Microelectronics, a time-of-flight ranging system integrated into a compact module.
  L298N DC motor driver: 2x DC motor driver with 78M05 positive voltage regulator (7..35 V) L298N: max 46 V, 2 A Set 5 V Enable jumper to enable 5 V regultor (needed for the L298N) and +5 V output at screw terminal or supply external +5 V at screw terminal Set ENA and/or ENB to +5 V to enable motor permanently or supply ENA and/or ENB with PWM signal IN1 and IN2 set rotation directory for motor A (OUT1/OUT2) IN2 and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
